// Logisim project CPU.circ as structural Verilog: 1 circuit, main circuit main
module main (
);

  wire clock_1_out;
  wire [7:0] adder_1_out, register_1_q;

  Clock clock_1 (.out(clock_1_out));
  Adder adder_1 (.a(8'h1), .b(register_1_q), .out(adder_1_out));  // open: cin, cout
  Register register_1 (.D(adder_1_out), .Q(register_1_q), .clk(clock_1_out));  // open: en, clr
  RAM #(.dataWidth(32)) ram_1 (.addr(register_1_q));  // open: data, sel, clk, ld, clr
endmodule
