// Logisim project CU.circ as structural Verilog: 1 circuit, main circuit main
module main (
  input  [31:0] \Instrucción ,
  output sel_jump,
  output jump,
  output [23:0] add_jump,
  output [23:0] add_branch
);

  wire and_1_out, and_2_out, BEQ, BNE, comparator_4_eq, not_1_out;

  Comparator #(.width(6)) comparator_1 (.a(\Instrucción [31:26]), .b(6'b000010), .eq(jump));  // open: gt, lt
  Comparator #(.width(6)) comparator_2 (.a(\Instrucción [31:26]), .b(6'b000100), .eq(BEQ));  // open: gt, lt
  Comparator #(.width(6)) comparator_3 (.a(\Instrucción [31:26]), .b(6'b000101), .eq(BNE));  // open: gt, lt
  Comparator #(.width(5)) comparator_4 (
    .a(\Instrucción [25:21]), .b(\Instrucción [20:16]), .eq(comparator_4_eq));  // open: gt, lt
  not not_1 (not_1_out, comparator_4_eq);
  Bit_Extender #(.in_width(26), .out_width(24)) bit_extender_1 (.in(\Instrucción [25:0]), .out(add_jump));
  assign add_branch = {{8{1'b0}}, \Instrucción [15:0]};  // Bit_Extender bit_extender_2
  and and_1 (and_1_out, comparator_4_eq, BEQ);
  and and_2 (and_2_out, BNE, not_1_out);
  or or_1 (sel_jump, and_1_out, jump, and_2_out);

  // Other names for the same wires on the sheet: add[15:0] = \Instrucción [15:0]; ta[25:0] = \Instrucción [25:0];
  //   rt[4:0] = \Instrucción [20:16]; rs[4:0] = \Instrucción [25:21]; op[5:0] = \Instrucción [31:26]

  // Notes on the sheet:
  //   Control Unit
endmodule
